// Logisim project circuit.circ as structural Verilog: 1 circuit, main circuit main
module main (
  input  _1,
  input  _2,
  input  _3,
  input  _4,
  input  _5,
  input  _6,
  input  _7,
  input  _8,
  input  _9,
  input  _10,
  input  _11,
  input  _12,
  input  _13
);

  wire and_1_out, demultiplexer_1_out0, demultiplexer_1_out1, even_parity_1_out, nand_1_out, nor_1_out,
       not_1_out, not_2_out, not_3_out, odd_parity_1_out, or_1_out, or_2_out;

  or or_1 (or_1_out, _3, _4);
  or or_2 (or_2_out, _9, _10);
  not not_1 (not_1_out, _13);
  nor nor_1 (nor_1_out, _5, _6, _7, _8);
  nand nand_1 (nand_1_out, _1, _1, _2, or_1_out, _4);
  and and_1 (and_1_out, _12, not_1_out);
  not not_2 (not_2_out, nand_1_out);
  xnor even_parity_1 (even_parity_1_out, not_2_out, _4, _5, nor_1_out, _9);
  Demultiplexer demultiplexer_1 (
    .out0(demultiplexer_1_out0), .out1(demultiplexer_1_out1), .in(or_2_out), .sel(_11), .en(_10));
  xor odd_parity_1 (odd_parity_1_out, _11, and_1_out);
  not not_3 (not_3_out, demultiplexer_1_out1);
  LED led_1 (.in(not_2_out));
  LED led_2 (.in(even_parity_1_out));
  LED led_3 (.in(nor_1_out));
  LED led_4 (.in(demultiplexer_1_out0));
  LED led_5 (.in(not_3_out));
  LED led_6 (.in(odd_parity_1_out));
endmodule
